# Fritzing sketch ESP8266WatchFritzing (saved by Fritzing 0.9.3b)

parts:
  U1 = NodeMCU V1.0
  Squix1 = OLED 0.96" 128x64 I2C SSD1306
  IC1 = DS1302 [package="DIP8 [THT]"]
  Y1 = CRYSTAL [package=tc38h]
  BAT1 = Battery Holders [package=battcom_20mm_pth]
  U2 = TOUCH [package=touch1]
  R1 = Rotary Potentiometer (Small) [maximum_resistance=100kΩ package=THT]
  U3 = LIPO-1000mAh [package=lipo-1000]

nets:
  N1: U1.D1, Squix1.SCL
  N2: U1.D2, Squix1.SCA
  3V3: U1.3V3, Squix1.VCC, IC1.+V, R1.leg1
  GND: U1.GND, Squix1.GND, IC1.0V, BAT1.-, R1.leg2, U3.-
  N3: U1.D5, IC1.SCLK_-_SPI_Clock
  N4: U1.D6, IC1.I/O_-_SPI_Data_In/Out
  N5: U1.D7, IC1.CE_-_Chip_Enable
  N6: U1.D8, U2.T2
  N7: U1.Vin, U3.+
  N8: U1.A0, R1.wiper
  N9: IC1.X1_-_Crystal, Y1.1
  N10: IC1.X2_-_Crystal, Y1.2
  N11: IC1.Vbat_-_Backup_Supply, BAT1.+

notes:
  DS1302时钟
  此处需要安装32768Hz晶体振荡器
  任意大小电池即可，建议容量800mAh，电压3.7V

custom parts:
  NodeMCU V1.0: ESP8266 based NodeMCU
